// Logisim project 04.01_Basic_Gates.circ as structural Verilog
module AND_Gate (
  input  A,
  input  B,
  output Y
);

  and and_1 (Y, A, B);
endmodule

module OR_Gate (
  input  A,
  input  B,
  output Y
);

  or or_1 (Y, A, B);
endmodule

module NOT_Gate (
  input  A,
  output Y
);

  not not_1 (Y, A);
endmodule

module NAND_Gate (
  input  A,
  input  B,
  output Y
);

  nand nand_1 (Y, A, B);
endmodule

module NOR_Gate (
  input  A,
  input  B,
  output Y
);

  nor nor_1 (Y, A, B);
endmodule

module XOR_Gate (
  input  A,
  input  B,
  output Y
);

  xor xor_1 (Y, A, B);
endmodule

module XNOR_Gate (
  input  A,
  input  B,
  output Y
);

  xnor xnor_1 (Y, A, B);
endmodule

module Buffer_Gate (
  input  A,
  output Y
);

  buf buffer_1 (Y, A);
endmodule
