// Logisim project 04.02_Univariate_Properties.circ as structural Verilog
module Identity_OR (
  input  A,
  output Y
);

  or or_1 (Y, A, 1'b0);
endmodule

module Identity_AND (
  input  A,
  output Y
);

  and and_1 (Y, A, 1'b1);
endmodule

module Idempotence_OR (
  input  A,
  output Y
);

  or or_1 (Y, A, A);
endmodule

module Idempotence_AND (
  input  A,
  output Y
);

  and and_1 (Y, A, A);
endmodule

module Annihilator_OR (
  input  A,
  output Y
);

  or or_1 (Y, A, 1'b1);
endmodule

module Annihilator_AND (
  input  A,
  output Y
);

  and and_1 (Y, A, 1'b0);
endmodule

module Complement_OR (
  input  A,
  output Y
);

  or or_1 (Y, A, ~A);  // OR_Gate
endmodule

module Complement_AND (
  input  A,
  output Y
);

  and and_1 (Y, A, ~A);  // AND_Gate
endmodule

module Involution (
  input  A,
  output Y
);

  wire not_1_out;

  not not_1 (not_1_out, A);
  not not_2 (Y, not_1_out);
endmodule
