// Logisim project 04.03_Multivariate_Properties.circ as structural Verilog
module Comm_OR (
  input  A,
  input  B,
  output Y1,
  output Y2
);

  or or_1 (Y1, A, B);
  or or_2 (Y2, B, A);
endmodule

module Comm_AND (
  input  A,
  input  B,
  output Y1,
  output Y2
);

  and and_1 (Y1, A, B);
  and and_2 (Y2, B, A);
endmodule

module Assoc_OR (
  input  A,
  input  B,
  input  C,
  output Y1,
  output Y2
);

  wire or_1_out, or_2_out;

  or or_1 (or_1_out, A, B);
  or or_2 (or_2_out, B, C);
  or or_3 (Y1, or_1_out, C);
  or or_4 (Y2, A, or_2_out);
endmodule

module Assoc_AND (
  input  A,
  input  B,
  input  C,
  output Y1,
  output Y2
);

  wire and_1_out, and_2_out;

  and and_1 (and_1_out, A, B);
  and and_2 (and_2_out, B, C);
  and and_3 (Y1, and_1_out, C);
  and and_4 (Y2, A, and_2_out);
endmodule

module Dist_AND_Over_OR (
  input  A,
  input  B,
  input  C,
  output Y1,
  output Y2
);

  wire and_1_out, or_1_out, or_2_out;

  and and_1 (and_1_out, B, C);
  or or_1 (or_1_out, A, B);
  or or_2 (or_2_out, A, C);
  or or_3 (Y1, A, and_1_out);
  and and_2 (Y2, or_1_out, or_2_out);
endmodule

module Dist_OR_Over_AND (
  input  A,
  input  B,
  input  C,
  output Y1,
  output Y2
);

  wire and_1_out, and_2_out, or_1_out;

  or or_1 (or_1_out, B, C);
  and and_1 (and_1_out, A, B);
  and and_2 (and_2_out, A, C);
  and and_3 (Y1, A, or_1_out);
  or or_2 (Y2, and_1_out, and_2_out);
endmodule

module Absorption_v1 (
  input  A,
  input  B,
  output Y
);

  wire and_1_out;

  and and_1 (and_1_out, A, B);
  or or_1 (Y, A, and_1_out);
endmodule

module Absorption_v2 (
  input  A,
  input  B,
  output Y
);

  wire or_1_out;

  or or_1 (or_1_out, A, B);
  and and_1 (Y, A, or_1_out);
endmodule

module Adjacency (
  input  A,
  input  B,
  output Y
);

  wire and_1_out, and_2_out;

  and and_1 (and_1_out, A, B);
  and and_2 (and_2_out, A, ~B);  // AND_Gate
  or or_1 (Y, and_1_out, and_2_out);
endmodule
