// Logisim project 04.06_Bool_Funcs.circ as structural Verilog: 5 circuits, main circuit main
module main (
  input  A,
  input  B,
  output Y1,
  output Y2
);

  nand nand_1 (Y1, A, B);
  or or_1 (Y2, ~A, ~B);  // OR_Gate
endmodule

module Define (
  input  A,
  input  B,
  output Y1,
  output Y2
);

  or or_1 (Y1, A, B);
  or or_2 (Y2, B, A);
endmodule

module Ex_1 (
  input  A,
  input  B,
  input  C,
  output Y
);

  wire nand_1_out;

  nand nand_1 (nand_1_out, B, C);
  nor nor_1 (Y, A, nand_1_out);

  // Notes on the sheet:
  //   (BC)'
  //   (A+(BC)')'
endmodule

module Ex_2 (
  input  A,
  input  B,
  input  C,
  output Y
);

  wire and_1_out, nand_1_out, nor_1_out;

  and and_1 (and_1_out, B, C);
  nand nand_1 (nand_1_out, B, ~C);  // NAND_Gate
  nor nor_1 (nor_1_out, A, and_1_out);
  nor nor_2 (Y, nor_1_out, nand_1_out);
endmodule

module Ex_2_Simplified (
  input  A,
  input  B,
  output Y
);

  and and_1 (Y, A, ~B);  // AND_Gate
endmodule
