// Logisim project 04.07_Func_Completeness.circ as structural Verilog: 2 circuits, main circuit main
module main (
  input  A,
  input  B,
  output Y
);

  wire and_1_out, or_1_out;

  and and_1 (and_1_out, A, B);
  and and_2 (Y, ~and_1_out, or_1_out);  // AND_Gate
  or or_1 (or_1_out, A, B);
endmodule

module Func_Completeness (
  input  in_1,
  input  in_2,
  output out_3
);

  and and_1 (out_3, in_1, in_2);
endmodule
