// Logisim project All_Circuits.circ as structural Verilog
module Ex_01 (
  input  J,
  input  B,
  input  P,
  output D
);

  wire and_1_out, and_2_out, and_3_out;

  and and_1 (and_1_out, J, B);
  and and_2 (and_2_out, B, P);
  and and_3 (and_3_out, P, J);
  or or_1 (D, and_1_out, and_2_out, and_3_out);
endmodule

module Ex_SOP (
  input  A,
  input  B,
  input  C,
  input  D,
  output Y
);

  wire and_1_out, and_2_out;

  and and_1 (and_1_out, ~A, B, ~C, D);  // AND_Gate
  or or_1 (Y, and_1_out, and_2_out);
  and and_2 (and_2_out, A, ~B, C, D);  // AND_Gate
endmodule

module Ex_POS (
  input  A,
  input  B,
  input  C,
  input  D,
  output Y
);

  wire or_1_out, or_2_out;

  or or_1 (or_1_out, ~A, B, ~C, D);  // OR_Gate
  and and_1 (Y, or_1_out, or_2_out);
  or or_2 (or_2_out, A, ~B, C, D);  // OR_Gate
endmodule

module Simp_Algebra_Ex01a (
  input  A,
  input  B,
  input  C,
  output Y
);

  wire and_1_out, and_2_out, and_3_out, or_1_out;

  and and_1 (and_1_out, A, B);
  or or_1 (or_1_out, B, C);
  and and_2 (and_2_out, B, C);
  or or_2 (Y, and_1_out, and_3_out);
  and and_3 (and_3_out, or_1_out, and_2_out);
endmodule

module Simp_Algebra_Ex01b (
  input  A,
  input  B,
  input  C,
  output Y
);

  wire and_1_out, and_2_out, and_3_out, or_1_out;

  and and_1 (and_1_out, A, B);
  or or_1 (or_1_out, B, C);
  and and_2 (and_2_out, B, C);
  or or_2 (Y, and_1_out, and_3_out);
  and and_3 (and_3_out, or_1_out, and_2_out);

  // Notes on the sheet:
  //   (AB)
  //   (B+C)
  //   (BC)
  //   BC(B+C)
  //   AB+BC(B+C)
endmodule
