// Logisim project All_Circuits.circ as structural Verilog: 1 circuit, main circuit Simple_Circuit_For_K_Map
module Simple_Circuit_For_K_Map (
  input  A,
  input  B,
  output Y
);

  wire and_1_out, and_2_out;

  and and_1 (and_1_out, A, B);
  or or_1 (Y, and_1_out, and_2_out);
  and and_2 (and_2_out, ~A, B);  // AND_Gate
endmodule
