// Logisim project Adder_Subtractor.circ as structural Verilog
module Half_Adder (
  input  A,
  input  B,
  output Sum,
  output COut
);

  xor U1 (Sum, A, B);
  and U2 (COut, A, B);
endmodule

module Full_Adder (
  input  CIn,
  input  A,
  input  B,
  output Sum,
  output COut
);

  wire U1_out, U2_out, U4_out;

  xor U1 (U1_out, A, B);
  and U2 (U2_out, A, B);
  xor U3 (Sum, CIn, U1_out);
  and U4 (U4_out, CIn, U1_out);
  or U5 (COut, U4_out, U2_out);
endmodule

module Adder_4_Bit (
  input  CIn,
  input  A0,
  input  B0,
  input  A1,
  input  B1,
  input  A2,
  input  B2,
  input  A3,
  input  B3,
  output Y0,
  output Y1,
  output Y2,
  output Y3,
  output COut
);

  wire full_adder_1_cout, full_adder_2_cout, full_adder_3_cout;

  Full_Adder full_adder_1 (.CIn(CIn), .A(A0), .B(B0), .Sum(Y0), .COut(full_adder_1_cout));
  Full_Adder full_adder_2 (.CIn(full_adder_1_cout), .A(A1), .B(B1), .Sum(Y1), .COut(full_adder_2_cout));
  Full_Adder full_adder_3 (.CIn(full_adder_2_cout), .A(A2), .B(B2), .Sum(Y2), .COut(full_adder_3_cout));
  Full_Adder full_adder_4 (.CIn(full_adder_3_cout), .A(A3), .B(B3), .Sum(Y3), .COut(COut));
endmodule

module Half_Subtractor (
  input  A,
  input  B,
  output Diff,
  output BOut
);

  xor xor_1 (Diff, A, B);
  and and_1 (BOut, ~A, B);  // AND_Gate
endmodule

module Full_Subtractor (
  input  BIn,
  input  A,
  input  B,
  output Diff,
  output BOut
);

  wire and_1_out, and_2_out, xor_1_out;

  xor xor_1 (xor_1_out, A, B);
  and and_1 (and_1_out, ~A, B);  // AND_Gate
  xor xor_2 (Diff, BIn, xor_1_out);
  and and_2 (and_2_out, BIn, ~xor_1_out);  // AND_Gate
  or or_1 (BOut, and_2_out, and_1_out);
endmodule

module Subtractor_4_Bit (
  input  A0,
  input  B0,
  input  A1,
  input  B1,
  input  A2,
  input  B2,
  input  A3,
  input  B3,
  output Y0,
  output Y1,
  output Y2,
  output Y3
);

  wire full_subtractor_1_bout, full_subtractor_2_bout, full_subtractor_3_bout;

  Full_Subtractor full_subtractor_1 (.A(A0), .B(B0), .Diff(Y0), .BOut(full_subtractor_1_bout));  // open: BIn
  Full_Subtractor full_subtractor_2 (
    .BIn(full_subtractor_1_bout), .A(A1), .B(B1), .Diff(Y1), .BOut(full_subtractor_2_bout));
  Full_Subtractor full_subtractor_3 (
    .BIn(full_subtractor_2_bout), .A(A2), .B(B2), .Diff(Y2), .BOut(full_subtractor_3_bout));
  Full_Subtractor full_subtractor_4 (.BIn(full_subtractor_3_bout), .A(A3), .B(B3), .Diff(Y3));  // open: BOut
endmodule

module Adder_Subtractor (
  input  Ctrl,
  input  A0,
  input  B0,
  input  A1,
  input  B1,
  input  A2,
  input  B2,
  input  A3,
  input  B3,
  output Y0,
  output Y1,
  output Y2,
  output Y3,
  output COut
);

  wire full_adder_1_cout, full_adder_2_cout, full_adder_3_cout, xor_1_out, xor_2_out, xor_3_out, xor_4_out;

  xor xor_1 (xor_1_out, Ctrl, B0);
  xor xor_2 (xor_2_out, Ctrl, B1);
  xor xor_3 (xor_3_out, Ctrl, B2);
  xor xor_4 (xor_4_out, Ctrl, B3);
  Full_Adder full_adder_1 (.CIn(Ctrl), .A(A0), .B(xor_1_out), .Sum(Y0), .COut(full_adder_1_cout));
  Full_Adder full_adder_2 (.CIn(full_adder_1_cout), .A(A1), .B(xor_2_out), .Sum(Y1), .COut(full_adder_2_cout));
  Full_Adder full_adder_3 (.CIn(full_adder_2_cout), .A(A2), .B(xor_3_out), .Sum(Y2), .COut(full_adder_3_cout));
  Full_Adder full_adder_4 (.CIn(full_adder_3_cout), .A(A3), .B(xor_4_out), .Sum(Y3), .COut(COut));

  // Notes on the sheet:
  //   Ctrl=0 to Add
  //   Ctrl=1 to Subtract
endmodule
