// Logisim project Encoders_Decoders.circ as structural Verilog
module Enc_3_Line_to_2_Bit (
  input  A,
  input  B,
  input  C,
  output [1:0] Y
);

  or U1 (Y[0], A, C);
  or U2 (Y[1], B, C);
endmodule

module Dec_2_Bit_to_4_Line (
  input  [1:0] A,
  output W,
  output X,
  output Y,
  output Z
);

  and U1 (W, ~A[0], ~A[1]);  // AND_Gate
  and U2 (X, A[0], ~A[1]);  // AND_Gate
  and U3 (Y, ~A[0], A[1]);  // AND_Gate
  and U4 (Z, A[0], A[1]);
endmodule
