// Logisim project Minterm_Generator.circ as structural Verilog
module Minterm_Generator (
  input  [2:0] A,
  output Y
);

  wire demultiplexer_1_out0, demultiplexer_1_out2, demultiplexer_1_out7;

  Demultiplexer #(.select(3), .enable("false")) demultiplexer_1 (
    .out0(demultiplexer_1_out0), .out2(demultiplexer_1_out2), .out7(demultiplexer_1_out7), .in(1'b1), .sel(A));  // open: out1, out3, out4, out5, out6
  or or_1 (Y, demultiplexer_1_out0, demultiplexer_1_out2, demultiplexer_1_out7);
endmodule
