// Logisim project Mux_Demux.circ as structural Verilog
module Simple_Mux (
  input  A,
  input  B,
  input  Sel,
  output Y
);

  Multiplexer #(.enable("false")) multiplexer_1 (.in0(A), .in1(B), .out(Y), .sel(Sel));
endmodule

module Simple_Demux (
  input  A,
  input  Sel,
  output Y,
  output Z
);

  Demultiplexer #(.enable("false")) demultiplexer_1 (.out0(Y), .out1(Z), .in(A), .sel(Sel));
endmodule

module Dmux_1_to_4 (
  input  [3:0] A,
  input  [1:0] Sel,
  output [3:0] W,
  output [3:0] X,
  output [3:0] Y,
  output [3:0] Z
);

  Demultiplexer #(.select(2), .width(4), .enable("false")) demultiplexer_1 (
    .out0(W), .out1(X), .out2(Y), .out3(Z), .in(A), .sel(Sel));
endmodule

module Minterm_Gen (
  input  [3:0] A,
  input  [1:0] Sel,
  output [3:0] V
);

  wire [3:0] demultiplexer_1_out1, demultiplexer_1_out2;

  Demultiplexer #(.select(2), .width(4), .enable("false")) demultiplexer_1 (
    .out1(demultiplexer_1_out1), .out2(demultiplexer_1_out2), .in(A), .sel(Sel));  // open: out0, out3
  assign V = demultiplexer_1_out1 | demultiplexer_1_out2;  // OR_Gate or_1, 4 bits wide
endmodule
