// Logisim project Parity.circ as structural Verilog
module Parity_Generator (
  input  [3:0] A,
  output [4:0] Y
);

  xor odd_parity_1 (Y[4], A[0], A[1], A[2], A[3]);

  assign Y[3:0] = A;
endmodule

module Hamming_Distance (
  input  [3:0] A,
  input  [3:0] B
);

  wire [2:0] bitadder_1_out;
  wire [3:0] xor_1_out;

  xor xor_1 (xor_1_out[0], A[0], B[0]);
  xor xor_2 (xor_1_out[1], A[1], B[1]);
  xor xor_3 (xor_1_out[2], A[2], B[2]);
  xor xor_4 (xor_1_out[3], A[3], B[3]);
  BitAdder #(.width(4)) bitadder_1 (.in0(xor_1_out), .out(bitadder_1_out));
  Hex_Digit_Display hex_digit_display_1 (.value({1'b0, bitadder_1_out}));  // open: dp
endmodule

module Hamming_Generator (
  input  [10:0] A,
  output [15:0] Y
);

  xor P0 (Y[15], A[10], A[9], A[7], A[6], A[4], A[2], A[0]);
  xor P1 (Y[14], A[10], A[8], A[7], A[5], A[4], A[1], A[0]);
  xor P2 (Y[12], A[9], A[8], A[7], A[3], A[2], A[1], A[0]);
  xor P3 (Y[8], A[6], A[5], A[4], A[3], A[2], A[1], A[0]);
  xor P4 (Y[0], Y[15], Y[14], A[10], Y[12], A[9], A[8], A[7], Y[8], A[6], A[5], A[4], A[3], A[2], A[1], A[0]);

  assign {Y[13], Y[11:9], Y[7:1]} = A;

  // Notes on the sheet:
  //   Input bit pattern is: D0-D1-D2
  //   D3-D4-D5-D6-D7-D8-D9-D10
endmodule

module Hamming_Check (
  input  [15:0] A,
  output Overall_Parity
);

  wire P0_out, P1_out, P2_out, P3_out, P4_out;
  wire [3:0] xor_2_out;

  xor P4 (P4_out, A[1], A[2], A[3], A[4], A[5], A[6], A[7], A[8], A[9], A[10], A[11], A[12], A[13], A[14], A[15]);
  xor P0 (P0_out, A[1], A[3], A[5], A[7], A[9], A[11], A[13]);
  xor P1 (P1_out, A[1], A[2], A[5], A[6], A[9], A[10], A[13]);
  xor P2 (P2_out, A[1], A[2], A[3], A[4], A[9], A[10], A[11]);
  xor P3 (P3_out, A[1], A[2], A[3], A[4], A[5], A[6], A[7]);
  xor xor_1 (Overall_Parity, A[0], P4_out);
  xor xor_2 (xor_2_out[0], P0_out, A[15]);
  xor xor_3 (xor_2_out[1], P1_out, A[14]);
  xor xor_4 (xor_2_out[2], P2_out, A[12]);
  xor xor_5 (xor_2_out[3], P3_out, A[8]);
  Hex_Digit_Display hex_digit_display_1 (.value(xor_2_out));  // open: dp

  // Notes on the sheet:
  //   Error Bit
endmodule
