// Logisim project Counters.circ as structural Verilog
module Two_Bit_Async (
  output Y0,
  output Y1
);

  wire Clk_out;

  Clock Clk (.out(Clk_out));
  J_K_Flip_Flop FF00 (.J(1'b1), .K(1'b1), .clk(Clk_out), .Q(Y0));  // open: Qn, preset, reset
  J_K_Flip_Flop FF01 (.J(1'b1), .K(1'b1), .clk(Y0), .Q(Y1));  // open: Qn, preset, reset
endmodule

module Three_Bit_Async (
  output Y0,
  output Y1,
  output Y2
);

  wire Clk_out;

  Clock Clk (.out(Clk_out));
  J_K_Flip_Flop FF00 (.J(1'b1), .K(1'b1), .clk(Clk_out), .Q(Y0));  // open: Qn, preset, reset
  J_K_Flip_Flop FF01 (.J(1'b1), .K(1'b1), .clk(Y0), .Q(Y1));  // open: Qn, preset, reset
  J_K_Flip_Flop FF02 (.J(1'b1), .K(1'b1), .clk(Y1), .Q(Y2));  // open: Qn, preset, reset
endmodule

module Four_Bit_Async (
  output Y0,
  output Y1,
  output Y2,
  output Y3
);

  wire Clk_out;

  Clock Clk (.out(Clk_out));
  J_K_Flip_Flop FF00 (.J(1'b1), .K(1'b1), .clk(Clk_out), .Q(Y0));  // open: Qn, preset, reset
  J_K_Flip_Flop FF01 (.J(1'b1), .K(1'b1), .clk(Y0), .Q(Y1));  // open: Qn, preset, reset
  J_K_Flip_Flop FF02 (.J(1'b1), .K(1'b1), .clk(Y1), .Q(Y2));  // open: Qn, preset, reset
  J_K_Flip_Flop FF03 (.J(1'b1), .K(1'b1), .clk(Y2), .Q(Y3));  // open: Qn, preset, reset
endmodule

module Two_Bit_Sync (
  output Y0,
  output Y1
);

  wire Clk_out;

  Clock Clk (.out(Clk_out));
  J_K_Flip_Flop FF00 (.J(1'b1), .K(1'b1), .clk(Clk_out), .Q(Y0));  // open: Qn, preset, reset
  J_K_Flip_Flop FF01 (.J(Y0), .K(Y0), .clk(Clk_out), .Q(Y1));  // open: Qn, preset, reset
endmodule

module Three_Bit_Sync (
  output Y0,
  output Y1,
  output Y2
);

  wire Clk_out, U1_out;

  J_K_Flip_Flop FF00 (.J(1'b1), .K(1'b1), .clk(Clk_out), .Q(Y0));  // open: Qn, preset, reset
  Clock Clk (.out(Clk_out));
  J_K_Flip_Flop FF01 (.J(Y0), .K(Y0), .clk(Clk_out), .Q(Y1));  // open: Qn, preset, reset
  and U1 (U1_out, Y0, Y1);
  J_K_Flip_Flop FF03 (.J(U1_out), .K(U1_out), .clk(Clk_out), .Q(Y2));  // open: Qn, preset, reset
endmodule

module Four_Bit_Sync_Up (
  output Y0,
  output Y1,
  output Y2,
  output Y03
);

  wire Clk_out, U1_out, U2_out;

  J_K_Flip_Flop FF00 (.J(1'b1), .K(1'b1), .clk(Clk_out), .Q(Y0));  // open: Qn, preset, reset
  Clock Clk (.out(Clk_out));
  J_K_Flip_Flop FF01 (.J(Y0), .K(Y0), .clk(Clk_out), .Q(Y1));  // open: Qn, preset, reset
  and U1 (U1_out, Y0, Y1);
  J_K_Flip_Flop FF02 (.J(U1_out), .K(U1_out), .clk(Clk_out), .Q(Y2));  // open: Qn, preset, reset
  and U2 (U2_out, U1_out, Y2);
  J_K_Flip_Flop FF03 (.J(U2_out), .K(U2_out), .clk(Clk_out), .Q(Y03));  // open: Qn, preset, reset
endmodule

module Four_Bit_Sync_Down (
  output Y0,
  output Y1,
  output Y2,
  output Y3
);

  wire and_1_out, and_2_out, Clk_out, FF0_qn, FF1_qn, FF2_qn;

  J_K_Flip_Flop FF0 (.J(1'b1), .K(1'b1), .clk(Clk_out), .Q(Y0), .Qn(FF0_qn));  // open: preset, reset
  Clock Clk (.out(Clk_out));
  J_K_Flip_Flop FF1 (.J(FF0_qn), .K(FF0_qn), .clk(Clk_out), .Q(Y1), .Qn(FF1_qn));  // open: preset, reset
  J_K_Flip_Flop FF2 (.J(and_1_out), .K(and_1_out), .clk(Clk_out), .Q(Y2), .Qn(FF2_qn));  // open: preset, reset
  and and_1 (and_1_out, FF1_qn, FF0_qn);
  and and_2 (and_2_out, FF2_qn, and_1_out);
  J_K_Flip_Flop FF3 (.J(and_2_out), .K(and_2_out), .clk(Clk_out), .Q(Y3));  // open: Qn, preset, reset
endmodule

module Four_Bit_Ring (
  output Y0,
  output Y1,
  output Y2,
  output Y3
);

  wire Clk_out, FF0_qn, FF1_qn, FF2_qn, FF3_qn, U1_out, U2_out;

  D_Flip_Flop FF0 (.D(U1_out), .clk(Clk_out), .Q(Y0), .Qn(FF0_qn));  // open: preset, reset
  or U1 (U1_out, Y3, U2_out);
  Clock Clk (.out(Clk_out));
  and U2 (U2_out, FF0_qn, FF1_qn, FF2_qn, FF3_qn);
  D_Flip_Flop FF1 (.D(Y0), .clk(Clk_out), .Q(Y1), .Qn(FF1_qn));  // open: preset, reset
  D_Flip_Flop FF2 (.D(Y1), .clk(Clk_out), .Q(Y2), .Qn(FF2_qn));  // open: preset, reset
  D_Flip_Flop FF3 (.D(Y2), .clk(Clk_out), .Q(Y3), .Qn(FF3_qn));  // open: preset, reset
endmodule

module Johnson (
  output Y0,
  output Y1,
  output Y2,
  output Y3
);

  wire Clk_out, FF3_qn;

  D_Flip_Flop FF0 (.D(FF3_qn), .clk(Clk_out), .Q(Y0));  // open: Qn, preset, reset
  Clock Clk (.out(Clk_out));
  D_Flip_Flop FF1 (.D(Y0), .clk(Clk_out), .Q(Y1));  // open: Qn, preset, reset
  D_Flip_Flop FF2 (.D(Y1), .clk(Clk_out), .Q(Y2));  // open: Qn, preset, reset
  D_Flip_Flop FF3 (.D(Y2), .clk(Clk_out), .Q(Y3), .Qn(FF3_qn));  // open: preset, reset
endmodule

module Decade (
  output Y0,
  output Y1,
  output Y2,
  output Y3
);

  wire Clk_out, U1_out, U2_out, U3_out;

  J_K_Flip_Flop FF0 (.J(1'b1), .K(1'b1), .clk(Clk_out), .Q(Y0), .reset(U3_out));  // open: Qn, preset
  Clock Clk (.out(Clk_out));
  J_K_Flip_Flop FF1 (.J(Y0), .K(Y0), .clk(Clk_out), .Q(Y1), .reset(U3_out));  // open: Qn, preset
  and U1 (U1_out, Y0, Y1);
  J_K_Flip_Flop FF2 (.J(U1_out), .K(U1_out), .clk(Clk_out), .Q(Y2), .reset(U3_out));  // open: Qn, preset
  and U2 (U2_out, U1_out, Y2);
  J_K_Flip_Flop FF3 (.J(U2_out), .K(U2_out), .clk(Clk_out), .Q(Y3), .reset(U3_out));  // open: Qn, preset
  and U3 (U3_out, Y3, ~Y2, Y1, ~Y0);  // AND_Gate
endmodule

module Up_Down (
  input  Up_Dn,
  output Y0,
  output Y1,
  output Y2,
  output Y3
);

  wire Clk_out, FF0_qn, FF1_qn, FF2_qn, not_1_out, U1_out, U2_out, U3_out, U4_out, U5_out, U6_out, U7_out,
       U8_out, U9_out;

  J_K_Flip_Flop FF0 (.J(1'b1), .K(1'b1), .clk(Clk_out), .Q(Y0), .Qn(FF0_qn));  // open: preset, reset
  Clock Clk (.out(Clk_out));
  not not_1 (not_1_out, Up_Dn);
  and U1 (U1_out, Up_Dn, Y0);
  J_K_Flip_Flop FF1 (.J(U4_out), .K(U4_out), .clk(Clk_out), .Q(Y1), .Qn(FF1_qn));  // open: preset, reset
  or U4 (U4_out, U1_out, U7_out);
  and U7 (U7_out, FF0_qn, not_1_out);
  and U2 (U2_out, U1_out, Y1);
  or U5 (U5_out, U2_out, U8_out);
  and U8 (U8_out, FF1_qn, U7_out);
  J_K_Flip_Flop FF2 (.J(U5_out), .K(U5_out), .clk(Clk_out), .Q(Y2), .Qn(FF2_qn));  // open: preset, reset
  and U3 (U3_out, U2_out, Y2);
  or U6 (U6_out, U3_out, U9_out);
  and U9 (U9_out, FF2_qn, U8_out);
  J_K_Flip_Flop FF3 (.J(U6_out), .K(U6_out), .clk(Clk_out), .Q(Y3));  // open: Qn, preset, reset
endmodule

module Freq_Div (
  output Y0,
  output Y1
);

  wire Clk_out;

  J_K_Flip_Flop FF0 (.J(1'b1), .K(1'b1), .clk(Clk_out), .Q(Y0));  // open: Qn, preset, reset
  Clock Clk (.out(Clk_out));
  J_K_Flip_Flop FF1 (.J(Y0), .K(Y0), .clk(Clk_out), .Q(Y1));  // open: Qn, preset, reset
endmodule
