// Logisim project Flip_Flops.circ as structural Verilog
module SR_Latch_NAND (
  input  S,
  input  E,
  input  R,
  output Q,
  output Q_Not
);

  wire U1_out, U2_out;

  nand U1 (U1_out, S, E);
  nand U2 (U2_out, E, R);
  nand U3 (Q, U1_out, Q_Not);
  nand U4 (Q_Not, Q, U2_out);
endmodule

module SR_Flip_Flop (
  input  S,
  input  R,
  output Q,
  output Q_Not
);

  wire Clk_out;

  S_R_Flip_Flop s_r_ff_1 (.S(S), .R(R), .clk(Clk_out), .Q(Q), .Qn(Q_Not));  // open: reset, preset
  Clock Clk (.out(Clk_out));
endmodule

module D_Latch_From_SR_Latch (
  input  D,
  output Q,
  output Q_Not
);

  wire Clk_out, not_1_out;

  S_R_Flip_Flop s_r_ff_1 (.S(D), .R(not_1_out), .clk(Clk_out), .Q(Q), .Qn(Q_Not));  // open: reset, preset
  not not_1 (not_1_out, D);
  Clock Clk (.out(Clk_out));
endmodule

module D_Flip_Flop (
  input  D,
  output Q,
  output Q_Not
);

  wire Clk_out;

  D_Flip_Flop_part d_ff_1 (.D(D), .clk(Clk_out), .Q(Q), .Qn(Q_Not));  // open: preset, reset
  Clock Clk (.out(Clk_out));
endmodule

module JK_Flip_Flop (
  input  J,
  input  K,
  output Q,
  output Q_Not
);

  wire Clk_out;

  J_K_Flip_Flop j_k_ff_1 (.J(J), .K(K), .clk(Clk_out), .Q(Q), .Qn(Q_Not));  // open: preset, reset
  Clock Clk (.out(Clk_out));
endmodule

module T_Flip_Flop (
  input  D,
  output Q,
  output Q_Not
);

  wire Clk_out;

  T_Flip_Flop_part t_ff_1 (.T(D), .clk(Clk_out), .Q(Q), .Qn(Q_Not));  // open: reset, preset
  Clock Clk (.out(Clk_out));
endmodule

module Master_Slave_FF (
  input  J,
  input  K,
  output Q,
  output Q_Not
);

  wire Clk_out, j_k_ff_1_q, j_k_ff_1_qn, not_1_out, U1_out, U2_out;

  Clock Clk (.out(Clk_out));
  J_K_Flip_Flop j_k_ff_1 (
    .J(U1_out), .K(U2_out), .clk(Clk_out), .Q(j_k_ff_1_q), .Qn(j_k_ff_1_qn));  // open: preset, reset
  and U1 (U1_out, J, Q_Not);
  and U2 (U2_out, Q, K);
  not not_1 (not_1_out, Clk_out);
  J_K_Flip_Flop j_k_ff_2 (.J(j_k_ff_1_q), .K(j_k_ff_1_qn), .clk(not_1_out), .Q(Q), .Qn(Q_Not));  // open: preset, reset
endmodule
