// Logisim project Registers.circ as structural Verilog
module Reg_From_D_FF (
  input  [3:0] DIn,
  output [3:0] DOut
);

  wire Clk_out;

  Clock Clk (.out(Clk_out));
  D_Flip_Flop d_ff_1 (.D(DIn[0]), .clk(Clk_out), .Q(DOut[0]));  // open: Qn, preset, reset
  D_Flip_Flop d_ff_2 (.D(DIn[1]), .clk(Clk_out), .Q(DOut[1]));  // open: Qn, preset, reset
  D_Flip_Flop d_ff_3 (.D(DIn[2]), .clk(Clk_out), .Q(DOut[2]));  // open: Qn, preset, reset
  D_Flip_Flop d_ff_4 (.D(DIn[3]), .clk(Clk_out), .Q(DOut[3]));  // open: Qn, preset, reset
endmodule

module Shift_Reg (
  input  D0,
  input  D1,
  input  D2,
  input  D3,
  input  Shift_Write,
  output SOut
);

  wire and_1_out, and_2_out, and_3_out, and_4_out, and_5_out, and_6_out, and_7_out, clock_1_out, FF0_q,
       FF1_q, FF2_q, not_1_out, or_1_out, or_2_out, or_3_out;

  not not_1 (not_1_out, Shift_Write);
  and and_1 (and_1_out, D0, not_1_out);
  Clock clock_1 (.out(clock_1_out));
  D_Flip_Flop FF0 (.D(and_1_out), .clk(clock_1_out), .Q(FF0_q));  // open: Qn, preset, reset
  and and_2 (and_2_out, D1, not_1_out);
  or or_1 (or_1_out, and_2_out, and_3_out);
  and and_3 (and_3_out, Shift_Write, FF0_q);
  D_Flip_Flop FF1 (.D(or_1_out), .clk(clock_1_out), .Q(FF1_q));  // open: Qn, preset, reset
  and and_4 (and_4_out, D2, not_1_out);
  and and_5 (and_5_out, Shift_Write, FF1_q);
  or or_2 (or_2_out, and_4_out, and_5_out);
  D_Flip_Flop FF2 (.D(or_2_out), .clk(clock_1_out), .Q(FF2_q));  // open: Qn, preset, reset
  and and_6 (and_6_out, D3, not_1_out);
  and and_7 (and_7_out, Shift_Write, FF2_q);
  or or_3 (or_3_out, and_6_out, and_7_out);
  D_Flip_Flop FF3 (.D(or_3_out), .clk(clock_1_out), .Q(SOut));  // open: Qn, preset, reset
endmodule
